// Logisim project MIPS2.circ as structural Verilog: 4 circuits, main circuit main
module main (
  input  in_1,
  input  Reset,
  output [2:0] out_3,
  output [15:0] Current_Instruction,
  output [7:0] PC_Value,
  output [3:0] out_6,
  output [3:0] out_7,
  output [3:0] out_8,
  output [3:0] out_9,
  output [3:0] out_10,
  output [1:0] out_11,
  output [3:0] out_12
);

  wire ALU_zf, and_1_out, clock_1_out, Control_aluscr, Control_branch, Control_jump, Control_megtoreg,
       Control_memread, Control_memwrite, Control_regdst, Control_regwrite, MemClock_out, RegClock_out;
  wire [7:0] adder_1_out, adder_2_out, multiplexer_3_out, multiplexer_4_out;

  Clock clock_1 (.out(clock_1_out));
  Register PC (.D(multiplexer_4_out), .Q(PC_Value), .clk(clock_1_out), .clr(Reset));  // open: en
  Adder adder_1 (.a(8'h1), .b(PC_Value), .out(adder_1_out));  // open: cin, cout
  Control Control (
    .OP3(Current_Instruction[15]), .OP2(Current_Instruction[14]), .OP1(Current_Instruction[13]),
    .OP0(Current_Instruction[12]), .s1(out_11[1]), .S0(out_11[0]), .RegDST(Control_regdst),
    .ALUSCR(Control_aluscr), .MegToReg(Control_megtoreg), .RegWrite(Control_regwrite),
    .MemRead(Control_memread), .MemWrite(Control_memwrite), .Branch(Control_branch), .Jump(Control_jump));
  ROM #(.dataWidth(16)) rom_1 (.addr(PC_Value), .data(Current_Instruction));  // open: sel
  Adder adder_2 (.a(adder_1_out), .b({{2{in_1}}, Current_Instruction[5:0]}), .out(adder_2_out));  // open: cin, cout
  Clock RegClock (.out(RegClock_out));
  Multiplexer #(.width(4), .enable("false")) multiplexer_1 (
    .in0(out_8), .in1(Current_Instruction[5:2]), .out(out_9), .sel(Control_aluscr));
  ALU ALU (.ALU_B(out_9), .ALU_A(out_10), .ALUS(out_11), .ZF(ALU_zf), .ALUO(out_12));
  Multiplexer #(.width(3), .enable("false")) multiplexer_2 (
    .in0(Current_Instruction[8:6]), .in1(Current_Instruction[5:3]), .out(out_3), .sel(Control_regdst));
  Reg2 reg2_1 (
    .RegWrite(Control_regwrite), .CLK(RegClock_out), .WriteSelect(out_3),
    .ReadReg1(Current_Instruction[11:9]), .ReadReg2(Current_Instruction[8:6]), .writeData(out_6),
    .ReadData1(out_10), .ReadData2(out_8));
  Multiplexer #(.width(8), .enable("false")) multiplexer_3 (
    .in0(adder_1_out), .in1(adder_2_out), .out(multiplexer_3_out), .sel(and_1_out));
  Multiplexer #(.width(8), .enable("false")) multiplexer_4 (
    .in0(multiplexer_3_out), .in1(Current_Instruction[11:4]), .out(multiplexer_4_out), .sel(Control_jump));
  and and_1 (and_1_out, Control_branch, ALU_zf);
  Multiplexer #(.width(4), .enable("false")) multiplexer_5 (
    .in0(out_12), .in1(out_7), .out(out_6), .sel(Control_megtoreg));
  RAM #(.addrWidth(4), .dataWidth(4), .bus("separate")) ram_1 (
    .addr(out_12), .din(out_8), .data(out_7), .str(Control_memwrite), .sel(1'b1), .clk(MemClock_out),
    .ld(Control_memread));  // open: clr
  Clock MemClock (.out(MemClock_out));

  // Notes on the sheet:
  //   contents of rom_1 (hex, n*v repeats v):
  //   5054 5294 7298 96a0 b948 6948 a970 cdc4 2084 1044 5294 5158 5b88 8bb8 3045 5040 3045 4220
  //   ALUSCR
endmodule

module ALU (
  input  [3:0] ALU_B,
  input  [3:0] ALU_A,
  input  [1:0] ALUS,
  output ZF,
  output [3:0] ALUO
);

  wire or_2_out;
  wire [3:0] adder_1_out, and_1_out, or_1_out, subtractor_1_out;

  Adder #(.width(4)) adder_1 (.a(ALU_A), .b(ALU_B), .out(adder_1_out));  // open: cin, cout
  Subtractor #(.width(4)) subtractor_1 (.a(ALU_A), .b(ALU_B), .out(subtractor_1_out));  // open: bin, bout
  assign and_1_out = ALU_A & ALU_B;  // AND_Gate and_1, 4 bits wide
  assign or_1_out = ALU_A | ALU_B;  // OR_Gate or_1, 4 bits wide
  Multiplexer #(.select(2), .width(4), .enable("false")) multiplexer_1 (
    .in0(adder_1_out), .in1(subtractor_1_out), .in2(and_1_out), .in3(or_1_out), .out(ALUO), .sel(ALUS));
  or or_2 (or_2_out, ALUO[0], ALUO[1], ALUO[2], ALUO[3]);
  not not_1 (ZF, or_2_out);
endmodule

module Control (
  input  OP3,
  input  OP2,
  input  OP1,
  input  OP0,
  output s1,
  output S0,
  output RegDST,
  output ALUSCR,
  output MegToReg,
  output RegWrite,
  output MemRead,
  output MemWrite,
  output Branch,
  output Jump
);

  wire and_1_out, and_2_out, and_3_out, and_4_out, and_5_out, and_6_out, and_7_out, and_8_out, and_9_out,
       and_10_out, and_11_out, and_12_out, and_14_out, and_15_out, not_1_out, not_2_out, not_3_out, not_4_out;

  not not_1 (not_1_out, OP3);
  not not_2 (not_2_out, OP2);
  not not_3 (not_3_out, OP1);
  not not_4 (not_4_out, OP0);
  and and_1 (and_1_out, OP2, not_4_out);
  and and_2 (and_2_out, OP3, not_4_out);
  and and_3 (and_3_out, not_2_out, OP1, OP0);
  and and_4 (and_4_out, OP3, not_2_out, not_3_out);
  and and_5 (and_5_out, not_1_out, OP2, not_4_out);
  and and_6 (and_6_out, not_2_out, not_4_out);
  and and_7 (and_7_out, OP3, not_2_out, not_3_out);
  and and_8 (and_8_out, not_1_out, OP1, OP0);
  and and_9 (and_9_out, not_1_out, not_3_out);
  and and_10 (and_10_out, not_1_out, not_4_out);
  and and_11 (and_11_out, OP2, not_3_out);
  and and_12 (and_12_out, OP3, OP1, OP0);
  and and_13 (MegToReg, not_1_out, not_2_out);
  and and_14 (and_14_out, not_3_out, OP0);
  and and_15 (and_15_out, OP2, OP1);
  and and_16 (MemRead, not_1_out, not_2_out, not_3_out);
  and and_17 (MemWrite, not_1_out, not_2_out, not_4_out);
  and and_18 (Branch, not_1_out, not_2_out, OP1, OP0);
  and and_19 (Jump, not_1_out, not_3_out, not_4_out);
  or or_1 (s1, and_1_out, and_2_out);
  or or_2 (S0, and_3_out, and_4_out, and_5_out);
  or or_3 (RegDST, and_6_out, and_7_out, and_8_out);
  or or_4 (ALUSCR, and_9_out, and_10_out, and_11_out, and_12_out);
  or or_5 (RegWrite, OP3, and_14_out, and_15_out);
endmodule

module Reg2 (
  input  [3:0] writeData,
  input  RegWrite,
  input  CLK,
  input  [2:0] ReadReg1,
  input  [2:0] WriteSelect,
  input  [2:0] ReadReg2,
  output [3:0] ReadData1,
  output [3:0] ReadData2
);

  wire and_1_out, and_2_out, and_3_out, and_4_out, and_5_out, and_6_out, and_7_out, and_8_out, and_9_out,
       decoder_1_out0, decoder_1_out1, decoder_1_out2, decoder_1_out3, decoder_1_out4, decoder_1_out5,
       decoder_1_out6, decoder_1_out7;
  wire [3:0] register_1_q, register_2_q, register_3_q, register_4_q, register_5_q, register_6_q,
       register_7_q, register_8_q;

  Decoder #(.select(3), .enable("false")) decoder_1 (
    .out0(decoder_1_out0), .out1(decoder_1_out1), .out2(decoder_1_out2), .out3(decoder_1_out3),
    .out4(decoder_1_out4), .out5(decoder_1_out5), .out6(decoder_1_out6), .out7(decoder_1_out7),
    .sel(WriteSelect));
  and and_1 (and_1_out, RegWrite, CLK);
  and and_2 (and_2_out, and_1_out, decoder_1_out0);
  and and_3 (and_3_out, and_1_out, decoder_1_out1);
  and and_4 (and_4_out, and_1_out, decoder_1_out2);
  and and_5 (and_5_out, decoder_1_out3, and_1_out);
  and and_6 (and_6_out, decoder_1_out4, and_1_out);
  and and_7 (and_7_out, decoder_1_out5, and_1_out);
  and and_8 (and_8_out, decoder_1_out6, and_1_out);
  and and_9 (and_9_out, and_1_out, decoder_1_out7);
  Register #(.width(4)) register_1 (.D(writeData), .Q(register_1_q), .clk(and_2_out), .clr(1'b1));  // open: en
  Register #(.width(4)) register_2 (.D(writeData), .Q(register_2_q), .clk(and_3_out));  // open: en, clr
  Register #(.width(4)) register_3 (.D(writeData), .Q(register_3_q), .clk(and_4_out));  // open: en, clr
  Register #(.width(4)) register_4 (.D(writeData), .Q(register_4_q), .clk(and_5_out));  // open: en, clr
  Register #(.width(4)) register_5 (.D(writeData), .Q(register_5_q), .clk(and_6_out));  // open: en, clr
  Register #(.width(4)) register_6 (.D(writeData), .Q(register_6_q), .clk(and_7_out));  // open: en, clr
  Register #(.width(4)) register_7 (.D(writeData), .Q(register_7_q), .clk(and_8_out));  // open: en, clr
  Register #(.width(4)) register_8 (.D(writeData), .Q(register_8_q), .clk(and_9_out));  // open: en, clr
  Multiplexer #(.select(3), .width(4), .enable("false")) multiplexer_1 (
    .in0(register_1_q), .in1(register_2_q), .in2(register_3_q), .in3(register_4_q), .in4(register_5_q),
    .in5(register_6_q), .in6(register_7_q), .in7(register_8_q), .out(ReadData1), .sel(ReadReg1));
  Multiplexer #(.select(3), .width(4), .enable("false")) multiplexer_2 (
    .in0(register_1_q), .in1(register_2_q), .in2(register_3_q), .in3(register_4_q), .in4(register_5_q),
    .in5(register_6_q), .in6(register_7_q), .in7(register_8_q), .out(ReadData2), .sel(ReadReg2));
endmodule
