// Logisim project Control.circ as structural Verilog: 1 circuit, main circuit main
module main (
  input  A,
  input  B,
  input  C,
  input  D,
  output s1,
  output S0,
  output RegDST,
  output ALUSCR,
  output MegToReg,
  output RegWrite,
  output MemRead,
  output MemWrite,
  output Branch,
  output Jump
);

  wire and_1_out, and_2_out, and_3_out, and_4_out, and_5_out, and_6_out, and_7_out, and_8_out, and_9_out,
       and_10_out, and_11_out, and_12_out, and_14_out, and_15_out, not_1_out, not_2_out, not_3_out, not_4_out;

  not not_1 (not_1_out, A);
  not not_2 (not_2_out, B);
  not not_3 (not_3_out, C);
  not not_4 (not_4_out, D);
  and and_1 (and_1_out, B, not_4_out);
  and and_2 (and_2_out, A, not_4_out);
  and and_3 (and_3_out, not_2_out, C, D);
  and and_4 (and_4_out, A, not_2_out, not_3_out);
  and and_5 (and_5_out, not_1_out, B, not_4_out);
  and and_6 (and_6_out, not_2_out, not_4_out);
  and and_7 (and_7_out, A, not_2_out, not_3_out);
  and and_8 (and_8_out, not_1_out, C, D);
  and and_9 (and_9_out, not_1_out, not_3_out);
  and and_10 (and_10_out, not_1_out, not_4_out);
  and and_11 (and_11_out, B, not_3_out);
  and and_12 (and_12_out, A, C, D);
  and and_13 (MegToReg, not_1_out, not_2_out);
  and and_14 (and_14_out, not_3_out, D);
  and and_15 (and_15_out, B, C);
  and and_16 (MemRead, not_1_out, not_2_out, not_3_out);
  and and_17 (MemWrite, not_1_out, not_2_out, not_4_out);
  and and_18 (Branch, not_1_out, not_2_out, C, D);
  and and_19 (Jump, not_1_out, not_3_out, not_4_out);
  or or_1 (s1, and_1_out, and_2_out);
  or or_2 (S0, and_3_out, and_4_out, and_5_out);
  or or_3 (RegDST, and_6_out, and_7_out, and_8_out);
  or or_4 (ALUSCR, and_9_out, and_10_out, and_11_out, and_12_out);
  or or_5 (RegWrite, A, and_14_out, and_15_out);
endmodule
