// Logisim project RegFile.circ as structural Verilog: 3 circuits, main circuit main
module main (
  input  [1:0] in_1,
  input  [1:0] in_2,
  input  [3:0] in_3,
  input  in_4,
  output out_5,
  output out_6,
  output [3:0] out_7
);

  assign {out_6, out_5} = in_1 ^ in_2;  // XOR_Gate xor_1, 2 bits wide
  Register #(.width(4)) register_1 (.D(in_3), .Q(out_7), .clk(in_4));  // open: en, clr
endmodule

module regF (
  input  [3:0] writeData,
  input  ZERO,
  input  RegWrite,
  input  [2:0] WriteSelect,
  input  [2:0] ReadReg1,
  input  [2:0] ReadReg2,
  output [3:0] ReadData1,
  output [3:0] ReadData2
);

  wire ClockSelect_clock0, ClockSelect_clock1, ClockSelect_clock2, ClockSelect_clock3, ClockSelect_clock4,
       ClockSelect_clock5, ClockSelect_clock6, ClockSelect_clock7;
  wire [3:0] register_1_q, register_2_q, register_3_q, register_4_q, register_5_q, register_6_q,
       register_7_q, register_8_q;

  RegClock ClockSelect (
    .RegWrite(RegWrite), .SelectIN(WriteSelect), .WriteData(writeData), .Q0(register_1_q), .Q1(register_2_q),
    .Q2(register_3_q), .Q3(register_4_q), .Q4(register_5_q), .Q5(register_6_q), .Q6(register_7_q),
    .Q7(register_8_q), .clock0(ClockSelect_clock0), .clock1(ClockSelect_clock1), .clock2(ClockSelect_clock2),
    .clock3(ClockSelect_clock3), .clock4(ClockSelect_clock4), .clock5(ClockSelect_clock5),
    .clock6(ClockSelect_clock6), .clock7(ClockSelect_clock7));
  Register #(.width(4)) register_1 (.D(writeData), .Q(register_1_q), .clk(ClockSelect_clock0), .clr(ZERO));  // open: en
  Register #(.width(4)) register_2 (.D(writeData), .Q(register_2_q), .clk(ClockSelect_clock1));  // open: en, clr
  Register #(.width(4)) register_3 (.D(writeData), .Q(register_3_q), .clk(ClockSelect_clock2));  // open: en, clr
  Register #(.width(4)) register_4 (.D(writeData), .Q(register_4_q), .clk(ClockSelect_clock3));  // open: en, clr
  Register #(.width(4)) register_5 (.D(writeData), .Q(register_5_q), .clk(ClockSelect_clock4));  // open: en, clr
  Register #(.width(4)) register_6 (.D(writeData), .Q(register_6_q), .clk(ClockSelect_clock5));  // open: en, clr
  Register #(.width(4)) register_7 (.D(writeData), .Q(register_7_q), .clk(ClockSelect_clock6));  // open: en, clr
  Register #(.width(4)) register_8 (.D(writeData), .Q(register_8_q), .clk(ClockSelect_clock7));  // open: en, clr
  Multiplexer #(.select(3), .width(4), .enable("false")) multiplexer_1 (
    .in0(register_1_q), .in1(register_2_q), .in2(register_3_q), .in3(register_4_q), .in4(register_5_q),
    .in5(register_6_q), .in6(register_7_q), .in7(register_8_q), .out(ReadData1), .sel(ReadReg1));
  Multiplexer #(.select(3), .width(4), .enable("false")) multiplexer_2 (
    .in0(register_1_q), .in1(register_2_q), .in2(register_3_q), .in3(register_4_q), .in4(register_5_q),
    .in5(register_6_q), .in6(register_7_q), .in7(register_8_q), .out(ReadData2), .sel(ReadReg2));
endmodule

module RegClock (
  input  [3:0] Q2,
  input  [3:0] WriteData,
  input  [3:0] Q0,
  input  [3:0] Q1,
  input  [3:0] Q3,
  input  [3:0] Q4,
  input  [3:0] Q5,
  input  [3:0] Q6,
  input  [3:0] Q7,
  input  RegWrite,
  input  [2:0] SelectIN,
  output clock1,
  output clock2,
  output clock3,
  output clock5,
  output clock6,
  output clock7,
  output clock0,
  output clock4
);

  wire decoder_1_out0, decoder_1_out1, decoder_1_out2, decoder_1_out3, decoder_1_out4, decoder_1_out5,
       decoder_1_out6, decoder_1_out7, or_1_out, or_2_out, or_3_out, or_4_out, or_5_out, or_6_out, or_7_out,
       or_8_out;
  wire [3:0] xor_1_out, xor_2_out, xor_3_out, xor_4_out, xor_5_out, xor_6_out, xor_7_out, xor_8_out;

  Decoder #(.select(3), .enable("false")) decoder_1 (
    .out0(decoder_1_out0), .out1(decoder_1_out1), .out2(decoder_1_out2), .out3(decoder_1_out3),
    .out4(decoder_1_out4), .out5(decoder_1_out5), .out6(decoder_1_out6), .out7(decoder_1_out7), .sel(SelectIN));
  and and_1 (clock0, decoder_1_out0, RegWrite, or_1_out);
  assign xor_1_out = WriteData ^ Q0;  // XOR_Gate xor_1, 4 bits wide
  or or_1 (or_1_out, xor_1_out[3], xor_1_out[2], xor_1_out[1], xor_1_out[0]);
  assign xor_2_out = WriteData ^ Q1;  // XOR_Gate xor_2, 4 bits wide
  or or_2 (or_2_out, xor_2_out[3], xor_2_out[2], xor_2_out[1], xor_2_out[0]);
  and and_2 (clock1, decoder_1_out1, RegWrite, or_2_out);
  assign xor_3_out = WriteData ^ Q2;  // XOR_Gate xor_3, 4 bits wide
  or or_3 (or_3_out, xor_3_out[3], xor_3_out[2], xor_3_out[1], xor_3_out[0]);
  and and_3 (clock2, decoder_1_out2, RegWrite, or_3_out);
  assign xor_4_out = WriteData ^ Q3;  // XOR_Gate xor_4, 4 bits wide
  or or_4 (or_4_out, xor_4_out[3], xor_4_out[2], xor_4_out[1], xor_4_out[0]);
  and and_4 (clock3, decoder_1_out3, RegWrite, or_4_out);
  assign xor_5_out = WriteData ^ Q4;  // XOR_Gate xor_5, 4 bits wide
  or or_5 (or_5_out, xor_5_out[3], xor_5_out[2], xor_5_out[1], xor_5_out[0]);
  and and_5 (clock4, decoder_1_out4, RegWrite, or_5_out);
  assign xor_6_out = WriteData ^ Q5;  // XOR_Gate xor_6, 4 bits wide
  and and_6 (clock5, decoder_1_out5, RegWrite, or_6_out);
  or or_6 (or_6_out, xor_6_out[3], xor_6_out[2], xor_6_out[1], xor_6_out[0]);
  assign xor_7_out = WriteData ^ Q6;  // XOR_Gate xor_7, 4 bits wide
  or or_7 (or_7_out, xor_7_out[3], xor_7_out[2], xor_7_out[1], xor_7_out[0]);
  and and_7 (clock6, decoder_1_out6, RegWrite, or_7_out);
  assign xor_8_out = WriteData ^ Q7;  // XOR_Gate xor_8, 4 bits wide
  or or_8 (or_8_out, xor_8_out[3], xor_8_out[2], xor_8_out[1], xor_8_out[0]);
  and and_8 (clock7, decoder_1_out7, RegWrite, or_8_out);
endmodule
