// Logisim project Test.circ as structural Verilog: 1 circuit, main circuit main
module main (
  input  [3:0] ALU_B,
  input  [3:0] ALU_A,
  input  [1:0] ALUS,
  output [3:0] ALUO
);

  wire [3:0] adder_1_out, and_1_out, or_1_out, subtractor_1_out;

  Adder #(.width(4)) adder_1 (.a(ALU_A), .b(ALU_B), .out(adder_1_out));  // open: cin, cout
  Subtractor #(.width(4)) subtractor_1 (.a(ALU_A), .b(ALU_B), .out(subtractor_1_out));  // open: bin, bout
  assign and_1_out = ALU_A & ALU_B;  // AND_Gate and_1, 4 bits wide
  assign or_1_out = ALU_A | ALU_B;  // OR_Gate or_1, 4 bits wide
  Multiplexer #(.select(2), .width(4), .enable("false")) multiplexer_1 (
    .in0(adder_1_out), .in1(subtractor_1_out), .in2(and_1_out), .in3(or_1_out), .out(ALUO), .sel(ALUS));
endmodule
